# Fritzing sketch Device3 (saved by Fritzing 0.9.0b)
breadboards: 1

parts:
  Part1 = Arduino Uno (Rev3)
  pH_Circuit1 = pH Circuit
  Conductivity_Circuit1 = Conductivity Circuit
  D_O_Circuit1 = D.O. Circuit
  U2 = TMP102 [package=sot563]
  U3 = RELAY [package=relay-jzc]
  J1 = Infrared Proximity Sensor
  Pre-Assembled_Female_BNC1 = Pre-Assembled Female BNC
  Pre-Assembled_Female_BNC2 = Pre-Assembled Female BNC
  Pre-Assembled_Female_BNC3 = Pre-Assembled Female BNC
  Part2 = Arduino Ethernet Shield (Rev3)

nets:
  N1: Part1.D5_PWM, U3.NO
  N2: Part1.D6_PWM, J1.Vout
  N3: Part1.D7, U2.ADD0
  VCC: Part1.5V, pH_Circuit1.Vcc, Conductivity_Circuit1.Vcc, D_O_Circuit1.Vcc, U2.VCC, U3.NC, J1.Vcc, Pre-Assembled_Female_BNC1.NC, Pre-Assembled_Female_BNC2.NC, Pre-Assembled_Female_BNC3.NC
  GND: Part1.GND, pH_Circuit1.GND#0, Conductivity_Circuit1.GND#0, D_O_Circuit1.GND#0, U2.SDA, U3.COIL2, J1.GND
  N4: pH_Circuit1.TX, Conductivity_Circuit1.TX, D_O_Circuit1.TX, Part2.A4/SDA
  N5: pH_Circuit1.RX, Conductivity_Circuit1.RX, D_O_Circuit1.RX, Part2.A5/SCL
  N6: pH_Circuit1.PRB, Pre-Assembled_Female_BNC2.PRB
  N7: pH_Circuit1.GND#5, Pre-Assembled_Female_BNC2.GND
  N8: Conductivity_Circuit1.PRB, Pre-Assembled_Female_BNC3.PRB
  N9: Conductivity_Circuit1.GND#5, Pre-Assembled_Female_BNC3.GND
  N10: D_O_Circuit1.PRB, Pre-Assembled_Female_BNC1.PRB
  N11: D_O_Circuit1.GND#5, Pre-Assembled_Female_BNC1.GND

notes:
  Relay 1 (Heater)
  DO Meter
  pH Meter
  EC Meter
  Fill Level Meter
  Temperature Sensor
  Cat 5 Cable
  Device 3
  RO Tank
  All wires other than Cat5 and Relay Output wires are 22AWG wire
