# Fritzing sketch Device4 (saved by Fritzing 0.9.0b)
breadboards: 1

parts:
  Part1 = Arduino Uno (Rev3)
  Conductivity_Circuit1 = Conductivity Circuit
  J1 = Infrared Proximity Sensor
  Pre-Assembled_Female_BNC3 = Pre-Assembled Female BNC
  Part2 = Arduino Ethernet Shield (Rev3)

nets:
  N1: Part1.D6_PWM, J1.Vout
  VCC: Part1.5V, Conductivity_Circuit1.Vcc, J1.Vcc, Pre-Assembled_Female_BNC3.NC
  GND: Part1.GND, Conductivity_Circuit1.GND#0, J1.GND
  N2: Conductivity_Circuit1.TX, Part2.A5/SCL
  N3: Conductivity_Circuit1.RX, Part2.A4/SDA
  N4: Conductivity_Circuit1.PRB, Pre-Assembled_Female_BNC3.PRB
  N5: Conductivity_Circuit1.GND#5, Pre-Assembled_Female_BNC3.GND

notes:
  EC Meter
  Fill Level Meter
  Cat 5 Cable
  Device 4
  Hold Tank
  All wires other than Cat5 and Relay Output wires are 22AWG wire
