# Fritzing sketch Device5 (saved by Fritzing 0.9.0b)
breadboards: 1

parts:
  Part1 = Arduino Uno (Rev3)
  U3 = RELAY [package=relay-jzc]
  U4 = RELAY [package=relay-jzc]
  Part2 = Arduino Ethernet Shield (Rev3)
  Q1 = LTR-301 [package=ltr-301]
  R1 = Resistor [tolerance=±5% resistance=330 package=THT]
  R2 = Resistor [tolerance=±5% resistance=10k package=THT]
  R3 = Resistor [tolerance=±5% resistance=10k package=THT]
  C1 = Electrolytic Capacitor [capacitance=1µF package="100 mil [THT, electrolytic]"]

nets:
  N1: Part1.D4, U4.NO
  N2: Part1.D5_PWM, U3.NO
  N3: Part1.5V, U3.NC, U4.NC, R2.Pin_0
  N4: Part1.GND, U3.COIL2, U4.COIL2, R3.Pin_0, C1.-
  N5: Part2.A1, Q1.E, R1.Pin_1
  N6: Q1.C, R1.Pin_0, R2.Pin_1, R3.Pin_1, C1.+

notes:
  Relay 1 (FCU)
  CT Sensor 1 (FCU)
  Relay 2 (Chiller)
  Cat 5 Cable
  Device 5
  HVAC
  All wires other than Cat5 and Relay Output wires are 22AWG wire
