# Fritzing sketch SoilMoisture PCB (saved by Fritzing 0.9.2b)
circuit board: 10.8382cm x 8.52025cm

parts:
  Part1 = Arduino Mega 2560 (Rev3)
  IC1 = Voltage Regulator [package=to220-igo]
  U2 = 3.5mm Audio Jack [package=audio-jack]
  U3 = 3.5mm Audio Jack [package=audio-jack]
  U4 = 3.5mm Audio Jack [package=audio-jack]
  U5 = 3.5mm Audio Jack [package=audio-jack]
  U6 = 3.5mm Audio Jack [package=audio-jack]
  U7 = 3.5mm Audio Jack [package=audio-jack]
  U8 = 3.5mm Audio Jack [package=audio-jack]
  U9 = 3.5mm Audio Jack [package=audio-jack]
  U10 = 3.5mm Audio Jack [package=audio-jack]
  U11 = 3.5mm Audio Jack [package=audio-jack]
  U12 = 3.5mm Audio Jack [package=audio-jack]
  U13 = 3.5mm Audio Jack [package=audio-jack]
  U14 = 3.5mm Audio Jack [package=audio-jack]
  U15 = 3.5mm Audio Jack [package=audio-jack]
  U16 = 3.5mm Audio Jack [part_number=14 package=audio-jack]
  U17 = 3.5mm Audio Jack [part_number=15 package=audio-jack]
  J1 = Power Jack [package=power_jack_pth_lock]
  Part2 = Analog Digital MUX Breakout

nets:
  N1: Part1.D20/SDA, Part1.SDA, Part2.SIG
  GND: Part1.GND, Part1.VIN, IC1.GND, IC1.OUT, U2.RIGHT, U2.SLEEVE, U3.RIGHT, U3.SLEEVE, U4.RIGHT, U4.SLEEVE, U5.RIGHT, U5.SLEEVE, U6.RIGHT, U6.SLEEVE, U7.RIGHT, U7.SLEEVE, U8.RIGHT, U8.SLEEVE, U9.RIGHT, U9.SLEEVE, U10.RIGHT, U10.SLEEVE, U11.RIGHT, U11.SLEEVE, U12.RIGHT, U12.SLEEVE, U13.RIGHT, U13.SLEEVE, U14.RIGHT, U14.SLEEVE, U15.RIGHT, U15.SLEEVE, U16.RIGHT, U16.SLEEVE, U17.RIGHT, U17.SLEEVE, J1.GND, J1.GNDBREAK, Part2.GND, Part2.EN
  N2: Part1.D9_PWM, Part2.S3
  N3: Part1.D8_PWM, Part2.S2
  N4: Part1.IOREF, Part2.VCC
  N5: Part1.D6_PWM, Part2.S0
  N6: Part1.D7_PWM, Part2.S1
  N7: IC1.IN, J1.PWR
  N8: U2.LEFT, Part2.C0
  N9: U3.LEFT, Part2.C1
  N10: U4.LEFT, Part2.C2
  N11: U5.LEFT, Part2.C3
  N12: U6.LEFT, Part2.C4
  N13: U7.LEFT, Part2.C5
  N14: U8.LEFT, Part2.C6
  N15: U9.LEFT, Part2.C7
  N16: U10.LEFT, Part2.C8
  N17: U11.LEFT, Part2.C9
  N18: U12.LEFT, Part2.C10
  N19: U13.LEFT, Part2.C11
  N20: U14.LEFT, Part2.C12
  N21: U15.LEFT, Part2.C13
  N22: U16.LEFT, Part2.C14
  N23: U17.LEFT, Part2.C15
