# Fritzing sketch Temp-Hum PCB (saved by Fritzing 0.9.2b)
breadboards: 1

parts:
  Part1 = Humidity Temperature Sensor SHT15
  U1 = RJ45 Jack [package=rj45-8]

nets:
  N1: Part1.GND, U1.2
  N2: Part1.SCL, U1.4
  N3: Part1.SDA, U1.5
  N4: Part1.VCC, U1.1
